// Logisim project riscv.circ as structural Verilog: 16 circuits, main circuit main
module main (
  input  [31:0] read_value,
  input  [31:0] instruction,
  input  reset,
  output error,
  output [31:0] address,
  output [31:0] write_value,
  output [3:0] write_enable,
  output read,
  output [31:0] pc_out
);

  wire and_1_out, and_2_out, and_3_out, and_4_out, and_5_out, and_6_out, and_7_out, and_8_out, and_9_out,
       and_10_out, and_11_out, and_12_out, and_13_out, and_14_out, and_15_out, and_16_out, and_17_out,
       and_18_out, and_19_out, and_20_out, and_21_out, and_22_out, and_28_out, and_31_out, and_32_out,
       and_33_out, and_34_out, and_35_out, and_36_out, and_37_out, and_38_out, and_39_out, and_40_out,
       and_41_out, and_42_out, and_43_out, and_44_out, and_45_out, and_46_out, and_47_out, and_48_out,
       and_49_out, and_50_out, and_51_out, and_52_out, and_53_out, and_54_out, and_55_out, and_56_out,
       and_57_out, and_58_out, and_59_out, and_60_out, and_61_out, and_62_out, and_63_out, and_64_out,
       and_65_out, and_66_out, and_67_out, and_68_out, and_69_out, and_70_out, and_75_out, not_1_out,
       not_2_out, not_3_out, not_4_out, not_5_out, not_6_out, not_7_out, not_8_out, not_9_out, not_10_out,
       not_11_out, not_12_out, not_13_out, not_14_out, not_15_out, not_16_out, not_17_out, not_18_out,
       not_19_out, not_20_out, not_21_out, not_22_out, not_23_out, not_24_out, not_25_out, not_26_out,
       not_27_out, not_28_out, not_29_out, not_30_out, not_31_out, not_32_out, not_33_out, not_34_out,
       not_35_out, not_36_out, not_37_out, not_38_out, not_39_out, not_40_out, not_41_out, not_42_out,
       not_43_out, not_44_out, not_45_out, or_2_out, or_3_out, or_4_out, or_5_out, or_6_out, or_7_out,
       or_8_out, or_9_out, or_10_out, or_11_out, or_12_out, or_13_out, or_14_out, or_15_out, or_16_out;
  wire [4:0] mux5_1_out_4, mux5_2_out_4;
  wire [11:0] mux12_1_out_4, mux12_2_out_4, undriven;
  wire [31:0] alu_1_result, mux32_1_out_4, pc_1_out_5, select_register_1_out1, select_register_1_out2,
       sign_1_result;

  Clock clock_1 ();  // open: out
  or or_1 (error, not_1_out, and_48_out);
  not not_1 (not_1_out, and_1_out);
  and and_1 (and_1_out, instruction[0], instruction[1]);
  not not_2 (not_2_out, instruction[4]);
  not not_3 (not_3_out, instruction[5]);
  not not_4 (not_4_out, instruction[6]);
  not not_5 (not_5_out, instruction[4]);
  not not_6 (not_6_out, instruction[6]);
  not not_7 (not_7_out, instruction[6]);
  not not_8 (not_8_out, instruction[5]);
  not not_9 (not_9_out, instruction[6]);
  not not_10 (not_10_out, instruction[4]);
  mux5 mux5_1 (.in_2({5{1'b0}}), .in_3(instruction[11:7]), .in_1(and_34_out), .out_4(mux5_1_out_4));
  not not_11 (not_11_out, instruction[12]);
  and and_2 (and_2_out, not_11_out, not_12_out);
  not not_12 (not_12_out, instruction[13]);
  not not_13 (not_13_out, instruction[14]);
  and and_3 (and_3_out, instruction[12], not_14_out);
  not not_14 (not_14_out, instruction[13]);
  not not_15 (not_15_out, instruction[14]);
  not not_16 (not_16_out, instruction[12]);
  and and_4 (and_4_out, not_16_out, instruction[13]);
  not not_17 (not_17_out, instruction[14]);
  and and_5 (and_5_out, instruction[12], instruction[13]);
  not not_18 (not_18_out, instruction[14]);
  not not_19 (not_19_out, instruction[12]);
  and and_6 (and_6_out, not_19_out, not_20_out);
  not not_20 (not_20_out, instruction[13]);
  and and_7 (and_7_out, instruction[12], not_21_out);
  not not_21 (not_21_out, instruction[13]);
  not not_22 (not_22_out, instruction[12]);
  and and_8 (and_8_out, not_22_out, instruction[13]);
  and and_9 (and_9_out, instruction[12], instruction[13]);
  not not_23 (not_23_out, instruction[3]);
  not not_24 (not_24_out, instruction[2]);
  and and_10 (and_10_out, not_23_out, not_24_out);
  and and_11 (and_11_out, not_2_out, not_3_out);
  and and_12 (and_12_out, and_11_out, not_4_out);
  and and_13 (and_13_out, not_5_out, instruction[5]);
  and and_14 (and_14_out, and_13_out, not_6_out);
  and and_15 (and_15_out, instruction[4], instruction[5]);
  and and_16 (and_16_out, and_15_out, not_7_out);
  and and_17 (and_17_out, instruction[4], not_8_out);
  and and_18 (and_18_out, and_17_out, not_9_out);
  and and_19 (and_19_out, not_10_out, instruction[5]);
  and and_20 (and_20_out, and_19_out, instruction[6]);
  and and_21 (and_21_out, instruction[4], instruction[5]);
  and and_22 (and_22_out, and_21_out, instruction[6]);
  or or_2 (or_2_out, and_36_out, and_33_out);
  or or_3 (or_3_out, or_2_out, and_44_out);
  mux5 mux5_2 (.in_2(mux5_1_out_4), .in_3(instruction[24:20]), .in_1(or_3_out), .out_4(mux5_2_out_4));
  // AND_Gate and_23 has open pins: in0=and_2_out, in1=not_13_out, out=open
  // AND_Gate and_24 has open pins: in0=and_3_out, in1=not_15_out, out=open
  // AND_Gate and_25 has open pins: in0=and_4_out, in1=not_17_out, out=open
  // AND_Gate and_26 has open pins: in0=and_5_out, in1=not_18_out, out=open
  // AND_Gate and_27 has open pins: in0=and_6_out, in1=instruction[14], out=open
  and and_28 (and_28_out, and_7_out, instruction[14]);
  // AND_Gate and_29 has open pins: in0=and_8_out, in1=instruction[14], out=open
  // AND_Gate and_30 has open pins: in0=and_9_out, in1=instruction[14], out=open
  not not_25 (not_25_out, error);
  not not_26 (not_26_out, instruction[2]);
  and and_31 (and_31_out, instruction[3], not_26_out);
  and and_32 (and_32_out, instruction[3], instruction[2]);
  and and_33 (and_33_out, and_12_out, and_10_out);
  and and_34 (and_34_out, and_14_out, and_10_out);
  and and_35 (and_35_out, and_16_out, and_10_out);
  and and_36 (and_36_out, and_18_out, and_10_out);
  and and_37 (and_37_out, and_20_out, and_10_out);
  and and_38 (and_38_out, and_22_out, and_10_out);
  or or_4 (or_4_out, and_43_out, and_42_out);
  or or_5 (or_5_out, or_4_out, and_41_out);
  mux12 mux12_1 (
    .in_1(and_37_out), .in_3({instruction[31], instruction[7], instruction[30:25], instruction[11:8]}),
    .in_2({instruction[31:25], mux5_2_out_4}), .out_4(mux12_1_out_4));
  sign sign_1 (.unsign(instruction[14]), .read(write_enable), .value(read_value), .result(sign_1_result));
  and and_39 (and_39_out, 1'b1, not_25_out);
  and and_40 (and_40_out, not_25_out, 1'b0);
  pc pc_1 (.load(and_40_out), .reset(reset), .inc(and_39_out), .out_5(pc_1_out_5));  // open: in_4
  and and_41 (and_41_out, and_16_out, and_31_out);
  and and_42 (and_42_out, and_18_out, and_31_out);
  and and_43 (and_43_out, and_32_out, and_20_out);
  and and_44 (and_44_out, and_31_out, and_20_out);
  and and_45 (and_45_out, and_32_out, and_12_out);
  or or_6 (or_6_out, and_36_out, and_35_out);
  and and_46 (and_46_out, or_6_out, and_28_out);
  and and_47 (and_47_out, and_46_out, instruction[31]);
  and and_48 (and_48_out, and_33_out, and_5_out);
  select_register select_register_1 (
    .load2(and_54_out), .store(and_50_out), .load1(and_53_out), .rs2(instruction[24:20]),
    .rd(instruction[11:7]), .rs1(instruction[19:15]), .in1(sign_1_result), .out1(select_register_1_out1),
    .out2(select_register_1_out2));
  or or_7 (or_7_out, and_33_out, and_34_out);
  mux12 mux12_2 (.in_1(or_7_out), .in_3(mux12_1_out_4), .in_2(undriven), .out_4(mux12_2_out_4));
  buf and_49 (and_49_out, not_28_out);  // AND_Gate
  not not_27 (not_27_out, and_34_out);
  and and_50 (and_50_out, not_27_out, and_33_out);
  not not_28 (not_28_out, or_7_out);
  not not_29 (not_29_out, or_7_out);
  buf and_51 (and_51_out, not_29_out);  // AND_Gate
  buf and_52 (and_52_out, not_32_out);  // AND_Gate
  or or_8 (or_8_out, and_34_out, and_33_out);
  not not_30 (not_30_out, 1'b0);
  not not_31 (not_31_out, 1'b0);
  and and_53 (and_53_out, not_30_out, or_8_out);
  and and_54 (and_54_out, not_31_out, and_34_out);
  not not_32 (not_32_out, or_7_out);
  not not_33 (not_33_out, or_7_out);
  and and_55 (and_55_out, and_47_out, not_33_out);
  buf and_56 (and_56_out, not_34_out);  // AND_Gate
  ALU alu_1 (
    .b(select_register_1_out1), .mode0(and_49_out), .mode1(and_51_out), .sub(and_52_out), .arith(and_55_out),
    .logic0(and_56_out), .logic1(and_57_out), .a({{20{1'b0}}, mux12_2_out_4}), .result(alu_1_result));  // open: zero, neg
  not not_34 (not_34_out, or_7_out);
  not not_35 (not_35_out, or_7_out);
  buf and_57 (and_57_out, not_35_out);  // AND_Gate
  not not_36 (not_36_out, alu_1_result[1]);
  and and_58 (and_58_out, not_39_out, not_40_out);
  and and_59 (and_59_out, alu_1_result[0], not_41_out);
  and and_60 (and_60_out, not_42_out, alu_1_result[1]);
  not not_37 (not_37_out, not_36_out);
  not not_38 (not_38_out, not_36_out);
  not not_39 (not_39_out, alu_1_result[0]);
  not not_40 (not_40_out, alu_1_result[1]);
  not not_41 (not_41_out, alu_1_result[1]);
  not not_42 (not_42_out, alu_1_result[0]);
  and and_61 (and_61_out, alu_1_result[0], alu_1_result[1]);
  and and_62 (and_62_out, and_58_out, and_2_out);
  and and_63 (and_63_out, not_36_out, and_3_out);
  and and_64 (and_64_out, and_59_out, and_2_out);
  and and_65 (and_65_out, not_36_out, and_3_out);
  and and_66 (and_66_out, and_60_out, and_2_out);
  and and_67 (and_67_out, not_37_out, and_3_out);
  and and_68 (and_68_out, and_61_out, and_2_out);
  and and_69 (and_69_out, not_38_out, and_3_out);
  not not_43 (not_43_out, and_34_out);
  not not_44 (not_44_out, error);
  or or_9 (or_9_out, and_62_out, and_63_out);
  or or_10 (or_10_out, or_9_out, and_4_out);
  or or_11 (or_11_out, and_64_out, and_65_out);
  or or_12 (or_12_out, or_11_out, and_4_out);
  or or_13 (or_13_out, and_66_out, and_67_out);
  or or_14 (or_14_out, or_13_out, and_4_out);
  or or_15 (or_15_out, and_68_out, and_69_out);
  or or_16 (or_16_out, or_15_out, and_4_out);
  and and_70 (and_70_out, not_43_out, and_33_out);
  not not_45 (not_45_out, and_33_out);
  and and_71 (write_enable[0], not_44_out, or_10_out);
  and and_72 (write_enable[1], not_44_out, or_12_out);
  and and_73 (write_enable[2], not_44_out, or_14_out);
  and and_74 (write_enable[3], not_44_out, or_16_out);
  mux32 mux32_1 (.in_3({32{1'b0}}), .in_2(select_register_1_out2), .in_1(and_70_out), .out_4(mux32_1_out_4));
  and and_75 (and_75_out, not_45_out, 1'b0);
  mux32 mux32_2 (.in_3({32{1'b0}}), .in_2(alu_1_result), .in_1(error), .out_4(address));
  mux32 mux32_3 (.in_3({32{1'b0}}), .in_2(mux32_1_out_4), .in_1(error), .out_4(write_value));
  mux mux_1 (.in_2(and_75_out), .in_3(1'b0), .in_1(error), .out_4(read));
  mux32 mux32_4 (.in_3({32{1'b0}}), .in_2(pc_1_out_5), .in_1(error), .out_4(pc_out));

  // Notes on the sheet:
  //   input
  //   imm12
  //   imm20
  //   arith
  //   output
endmodule

module pc (
  input  reset,
  input  inc,
  input  load,
  input  [31:0] in_4,
  output [31:0] out_5
);

  wire and_1_out, and_2_out, and_3_out, and_4_out, and_5_out, and_6_out, and_7_out, and_8_out, and_9_out,
       and_10_out, and_11_out, and_12_out, and_13_out, and_14_out, and_15_out, and_16_out, and_17_out,
       and_18_out, and_19_out, and_20_out, and_21_out, and_22_out, and_23_out, and_24_out, and_25_out,
       and_26_out, and_27_out, and_28_out, and_29_out, and_30_out, and_31_out, and_32_out, and_33_out,
       and_34_out, and_35_out, and_36_out, and_37_out, and_38_out, and_39_out, and_40_out, and_41_out,
       and_42_out, and_43_out, and_44_out, and_45_out, and_46_out, and_47_out, and_48_out, and_49_out,
       and_50_out, and_51_out, and_52_out, and_53_out, and_54_out, and_55_out, and_56_out, and_57_out,
       and_58_out, and_59_out, and_60_out, and_61_out, and_62_out, and_63_out, and_64_out, and_65_out,
       and_66_out, and_67_out, and_68_out, and_69_out, and_70_out, and_71_out, and_72_out, and_73_out,
       and_74_out, and_75_out, and_76_out, and_77_out, and_78_out, and_79_out, and_80_out, and_81_out,
       and_82_out, and_83_out, and_84_out, and_85_out, and_86_out, and_87_out, and_88_out, and_89_out,
       and_90_out, and_91_out, and_92_out, and_93_out, and_94_out, and_95_out, and_96_out, and_97_out,
       and_98_out, and_99_out, and_100_out, and_101_out, and_102_out, and_103_out, and_104_out, and_105_out,
       and_106_out, and_107_out, and_108_out, and_109_out, and_110_out, and_111_out, and_112_out,
       and_113_out, and_114_out, and_115_out, and_116_out, and_117_out, and_118_out, and_119_out,
       and_120_out, and_121_out, and_122_out, and_123_out, and_124_out, and_125_out, and_126_out,
       and_127_out, and_128_out, and_129_out, and_130_out, dff_1_out_2, dff_2_out_2, dff_3_out_2,
       dff_4_out_2, dff_5_out_2, dff_6_out_2, dff_7_out_2, dff_8_out_2, dff_9_out_2, dff_10_out_2,
       dff_11_out_2, dff_12_out_2, dff_13_out_2, dff_14_out_2, dff_15_out_2, dff_16_out_2, dff_17_out_2,
       dff_18_out_2, dff_19_out_2, dff_20_out_2, dff_21_out_2, dff_22_out_2, dff_23_out_2, dff_24_out_2,
       dff_25_out_2, dff_26_out_2, dff_27_out_2, dff_28_out_2, dff_29_out_2, dff_30_out_2, dff_31_out_2,
       dff_32_out_2, not_1_out, not_2_out, or_1_out, or_2_out, or_3_out, or_4_out, or_5_out, or_6_out,
       or_7_out, or_8_out, or_9_out, or_10_out, or_11_out, or_12_out, or_13_out, or_14_out, or_15_out,
       or_16_out, or_17_out, or_18_out, or_19_out, or_20_out, or_21_out, or_22_out, or_23_out, or_24_out,
       or_25_out, or_26_out, or_27_out, or_28_out, or_29_out, or_30_out, or_31_out, or_32_out;

  not not_1 (not_1_out, reset);
  Clock clock_1 ();  // open: out
  not not_2 (not_2_out, load);
  and and_1 (and_1_out, not_1_out, load);
  and and_2 (and_2_out, not_1_out, inc);
  and and_3 (and_3_out, and_2_out, not_2_out);
  and and_4 (and_4_out, and_1_out, in_4[0]);
  and and_5 (and_5_out, not_2_out, and_68_out);
  and and_6 (and_6_out, and_1_out, in_4[1]);
  and and_7 (and_7_out, not_2_out, and_69_out);
  and and_8 (and_8_out, and_1_out, in_4[2]);
  and and_9 (and_9_out, not_2_out, and_70_out);
  and and_10 (and_10_out, and_1_out, in_4[3]);
  and and_11 (and_11_out, not_2_out, and_71_out);
  and and_12 (and_12_out, and_1_out, in_4[4]);
  and and_13 (and_13_out, not_2_out, and_72_out);
  and and_14 (and_14_out, and_1_out, in_4[5]);
  and and_15 (and_15_out, not_2_out, and_73_out);
  and and_16 (and_16_out, and_1_out, in_4[6]);
  and and_17 (and_17_out, not_2_out, and_74_out);
  and and_18 (and_18_out, and_1_out, in_4[7]);
  and and_19 (and_19_out, not_2_out, and_75_out);
  and and_20 (and_20_out, and_1_out, in_4[8]);
  and and_21 (and_21_out, not_2_out, and_76_out);
  and and_22 (and_22_out, and_1_out, in_4[9]);
  and and_23 (and_23_out, not_2_out, and_77_out);
  and and_24 (and_24_out, and_1_out, in_4[10]);
  and and_25 (and_25_out, not_2_out, and_78_out);
  and and_26 (and_26_out, and_1_out, in_4[11]);
  and and_27 (and_27_out, not_2_out, and_79_out);
  and and_28 (and_28_out, and_1_out, in_4[12]);
  and and_29 (and_29_out, not_2_out, and_80_out);
  and and_30 (and_30_out, and_1_out, in_4[13]);
  and and_31 (and_31_out, not_2_out, and_81_out);
  and and_32 (and_32_out, and_1_out, in_4[14]);
  and and_33 (and_33_out, not_2_out, and_82_out);
  and and_34 (and_34_out, and_1_out, in_4[15]);
  and and_35 (and_35_out, not_2_out, and_83_out);
  and and_36 (and_36_out, and_1_out, in_4[16]);
  and and_37 (and_37_out, not_2_out, and_84_out);
  and and_38 (and_38_out, and_1_out, in_4[17]);
  and and_39 (and_39_out, not_2_out, and_85_out);
  and and_40 (and_40_out, and_1_out, in_4[18]);
  and and_41 (and_41_out, not_2_out, and_86_out);
  and and_42 (and_42_out, and_1_out, in_4[19]);
  and and_43 (and_43_out, not_2_out, and_87_out);
  and and_44 (and_44_out, and_1_out, in_4[20]);
  and and_45 (and_45_out, not_2_out, and_88_out);
  and and_46 (and_46_out, and_1_out, in_4[21]);
  and and_47 (and_47_out, not_2_out, and_89_out);
  and and_48 (and_48_out, and_1_out, in_4[22]);
  and and_49 (and_49_out, not_2_out, and_90_out);
  and and_50 (and_50_out, and_1_out, in_4[23]);
  and and_51 (and_51_out, not_2_out, and_91_out);
  and and_52 (and_52_out, and_1_out, in_4[24]);
  and and_53 (and_53_out, not_2_out, and_92_out);
  and and_54 (and_54_out, and_1_out, in_4[25]);
  and and_55 (and_55_out, not_2_out, and_93_out);
  and and_56 (and_56_out, and_1_out, in_4[26]);
  and and_57 (and_57_out, not_2_out, and_94_out);
  and and_58 (and_58_out, and_1_out, in_4[27]);
  and and_59 (and_59_out, not_2_out, and_95_out);
  and and_60 (and_60_out, and_1_out, in_4[28]);
  and and_61 (and_61_out, not_2_out, and_96_out);
  and and_62 (and_62_out, and_1_out, in_4[29]);
  and and_63 (and_63_out, not_2_out, and_97_out);
  and and_64 (and_64_out, and_1_out, in_4[30]);
  and and_65 (and_65_out, not_2_out, and_98_out);
  and and_66 (and_66_out, and_1_out, in_4[31]);
  and and_67 (and_67_out, not_2_out, and_99_out);
  or or_1 (or_1_out, and_4_out, and_5_out);
  or or_2 (or_2_out, and_6_out, and_7_out);
  or or_3 (or_3_out, and_8_out, and_9_out);
  or or_4 (or_4_out, and_10_out, and_11_out);
  or or_5 (or_5_out, and_12_out, and_13_out);
  or or_6 (or_6_out, and_14_out, and_15_out);
  or or_7 (or_7_out, and_16_out, and_17_out);
  or or_8 (or_8_out, and_18_out, and_19_out);
  or or_9 (or_9_out, and_20_out, and_21_out);
  or or_10 (or_10_out, and_22_out, and_23_out);
  or or_11 (or_11_out, and_24_out, and_25_out);
  or or_12 (or_12_out, and_26_out, and_27_out);
  or or_13 (or_13_out, and_28_out, and_29_out);
  or or_14 (or_14_out, and_30_out, and_31_out);
  or or_15 (or_15_out, and_32_out, and_33_out);
  or or_16 (or_16_out, and_34_out, and_35_out);
  or or_17 (or_17_out, and_36_out, and_37_out);
  or or_18 (or_18_out, and_38_out, and_39_out);
  or or_19 (or_19_out, and_40_out, and_41_out);
  or or_20 (or_20_out, and_42_out, and_43_out);
  or or_21 (or_21_out, and_44_out, and_45_out);
  or or_22 (or_22_out, and_46_out, and_47_out);
  or or_23 (or_23_out, and_48_out, and_49_out);
  or or_24 (or_24_out, and_50_out, and_51_out);
  or or_25 (or_25_out, and_52_out, and_53_out);
  or or_26 (or_26_out, and_54_out, and_55_out);
  or or_27 (or_27_out, and_56_out, and_57_out);
  or or_28 (or_28_out, and_58_out, and_59_out);
  or or_29 (or_29_out, and_60_out, and_61_out);
  or or_30 (or_30_out, and_62_out, and_63_out);
  or or_31 (or_31_out, and_64_out, and_65_out);
  or or_32 (or_32_out, and_66_out, and_67_out);
  dff dff_1 (.in_1(or_1_out), .out_2(dff_1_out_2));
  and and_68 (and_68_out, out_5[0], not_1_out);
  dff dff_2 (.in_1(or_2_out), .out_2(dff_2_out_2));
  and and_69 (and_69_out, out_5[1], not_1_out);
  dff dff_3 (.in_1(or_3_out), .out_2(dff_3_out_2));
  and and_70 (and_70_out, out_5[2], not_1_out);
  dff dff_4 (.in_1(or_4_out), .out_2(dff_4_out_2));
  and and_71 (and_71_out, out_5[3], not_1_out);
  dff dff_5 (.in_1(or_5_out), .out_2(dff_5_out_2));
  and and_72 (and_72_out, out_5[4], not_1_out);
  dff dff_6 (.in_1(or_6_out), .out_2(dff_6_out_2));
  and and_73 (and_73_out, out_5[5], not_1_out);
  dff dff_7 (.in_1(or_7_out), .out_2(dff_7_out_2));
  and and_74 (and_74_out, out_5[6], not_1_out);
  dff dff_8 (.in_1(or_8_out), .out_2(dff_8_out_2));
  and and_75 (and_75_out, out_5[7], not_1_out);
  dff dff_9 (.in_1(or_9_out), .out_2(dff_9_out_2));
  and and_76 (and_76_out, out_5[8], not_1_out);
  dff dff_10 (.in_1(or_10_out), .out_2(dff_10_out_2));
  and and_77 (and_77_out, out_5[9], not_1_out);
  dff dff_11 (.in_1(or_11_out), .out_2(dff_11_out_2));
  and and_78 (and_78_out, out_5[10], not_1_out);
  dff dff_12 (.in_1(or_12_out), .out_2(dff_12_out_2));
  and and_79 (and_79_out, out_5[11], not_1_out);
  dff dff_13 (.in_1(or_13_out), .out_2(dff_13_out_2));
  and and_80 (and_80_out, out_5[12], not_1_out);
  dff dff_14 (.in_1(or_14_out), .out_2(dff_14_out_2));
  and and_81 (and_81_out, out_5[13], not_1_out);
  dff dff_15 (.in_1(or_15_out), .out_2(dff_15_out_2));
  and and_82 (and_82_out, out_5[14], not_1_out);
  dff dff_16 (.in_1(or_16_out), .out_2(dff_16_out_2));
  and and_83 (and_83_out, out_5[15], not_1_out);
  dff dff_17 (.in_1(or_17_out), .out_2(dff_17_out_2));
  and and_84 (and_84_out, out_5[16], not_1_out);
  dff dff_18 (.in_1(or_18_out), .out_2(dff_18_out_2));
  and and_85 (and_85_out, out_5[17], not_1_out);
  dff dff_19 (.in_1(or_19_out), .out_2(dff_19_out_2));
  and and_86 (and_86_out, out_5[18], not_1_out);
  dff dff_20 (.in_1(or_20_out), .out_2(dff_20_out_2));
  and and_87 (and_87_out, out_5[19], not_1_out);
  dff dff_21 (.in_1(or_21_out), .out_2(dff_21_out_2));
  and and_88 (and_88_out, out_5[20], not_1_out);
  dff dff_22 (.in_1(or_22_out), .out_2(dff_22_out_2));
  and and_89 (and_89_out, out_5[21], not_1_out);
  dff dff_23 (.in_1(or_23_out), .out_2(dff_23_out_2));
  and and_90 (and_90_out, out_5[22], not_1_out);
  dff dff_24 (.in_1(or_24_out), .out_2(dff_24_out_2));
  and and_91 (and_91_out, out_5[23], not_1_out);
  dff dff_25 (.in_1(or_25_out), .out_2(dff_25_out_2));
  and and_92 (and_92_out, out_5[24], not_1_out);
  dff dff_26 (.in_1(or_26_out), .out_2(dff_26_out_2));
  and and_93 (and_93_out, out_5[25], not_1_out);
  dff dff_27 (.in_1(or_27_out), .out_2(dff_27_out_2));
  and and_94 (and_94_out, out_5[26], not_1_out);
  dff dff_28 (.in_1(or_28_out), .out_2(dff_28_out_2));
  and and_95 (and_95_out, out_5[27], not_1_out);
  dff dff_29 (.in_1(or_29_out), .out_2(dff_29_out_2));
  and and_96 (and_96_out, out_5[28], not_1_out);
  dff dff_30 (.in_1(or_30_out), .out_2(dff_30_out_2));
  and and_97 (and_97_out, out_5[29], not_1_out);
  dff dff_31 (.in_1(or_31_out), .out_2(dff_31_out_2));
  and and_98 (and_98_out, out_5[30], not_1_out);
  dff dff_32 (.in_1(or_32_out), .out_2(dff_32_out_2));
  and and_99 (and_99_out, out_5[31], not_1_out);
  xor xor_1 (out_5[0], dff_1_out_2, and_3_out);
  and and_100 (and_100_out, and_3_out, dff_1_out_2);
  xor xor_2 (out_5[1], dff_2_out_2, and_100_out);
  and and_101 (and_101_out, and_100_out, dff_2_out_2);
  xor xor_3 (out_5[2], dff_3_out_2, and_101_out);
  and and_102 (and_102_out, and_101_out, dff_3_out_2);
  xor xor_4 (out_5[3], dff_4_out_2, and_102_out);
  and and_103 (and_103_out, and_102_out, dff_4_out_2);
  xor xor_5 (out_5[4], dff_5_out_2, and_103_out);
  and and_104 (and_104_out, and_103_out, dff_5_out_2);
  xor xor_6 (out_5[5], dff_6_out_2, and_104_out);
  and and_105 (and_105_out, and_104_out, dff_6_out_2);
  xor xor_7 (out_5[6], dff_7_out_2, and_105_out);
  and and_106 (and_106_out, and_105_out, dff_7_out_2);
  xor xor_8 (out_5[7], dff_8_out_2, and_106_out);
  and and_107 (and_107_out, and_106_out, dff_8_out_2);
  xor xor_9 (out_5[8], dff_9_out_2, and_107_out);
  and and_108 (and_108_out, and_107_out, dff_9_out_2);
  xor xor_10 (out_5[9], dff_10_out_2, and_108_out);
  and and_109 (and_109_out, and_108_out, dff_10_out_2);
  xor xor_11 (out_5[10], dff_11_out_2, and_109_out);
  and and_110 (and_110_out, and_109_out, dff_11_out_2);
  xor xor_12 (out_5[11], dff_12_out_2, and_110_out);
  and and_111 (and_111_out, and_110_out, dff_12_out_2);
  xor xor_13 (out_5[12], dff_13_out_2, and_111_out);
  and and_112 (and_112_out, and_111_out, dff_13_out_2);
  xor xor_14 (out_5[13], dff_14_out_2, and_112_out);
  and and_113 (and_113_out, and_112_out, dff_14_out_2);
  xor xor_15 (out_5[14], dff_15_out_2, and_113_out);
  and and_114 (and_114_out, and_113_out, dff_15_out_2);
  xor xor_16 (out_5[15], dff_16_out_2, and_114_out);
  and and_115 (and_115_out, and_114_out, dff_16_out_2);
  xor xor_17 (out_5[16], dff_17_out_2, and_115_out);
  and and_116 (and_116_out, and_115_out, dff_17_out_2);
  xor xor_18 (out_5[17], dff_18_out_2, and_116_out);
  and and_117 (and_117_out, and_116_out, dff_18_out_2);
  xor xor_19 (out_5[18], dff_19_out_2, and_117_out);
  and and_118 (and_118_out, and_117_out, dff_19_out_2);
  xor xor_20 (out_5[19], dff_20_out_2, and_118_out);
  and and_119 (and_119_out, and_118_out, dff_20_out_2);
  xor xor_21 (out_5[20], dff_21_out_2, and_119_out);
  and and_120 (and_120_out, and_119_out, dff_21_out_2);
  xor xor_22 (out_5[21], dff_22_out_2, and_120_out);
  and and_121 (and_121_out, and_120_out, dff_22_out_2);
  xor xor_23 (out_5[22], dff_23_out_2, and_121_out);
  and and_122 (and_122_out, and_121_out, dff_23_out_2);
  xor xor_24 (out_5[23], dff_24_out_2, and_122_out);
  and and_123 (and_123_out, and_122_out, dff_24_out_2);
  xor xor_25 (out_5[24], dff_25_out_2, and_123_out);
  and and_124 (and_124_out, and_123_out, dff_25_out_2);
  xor xor_26 (out_5[25], dff_26_out_2, and_124_out);
  and and_125 (and_125_out, and_124_out, dff_26_out_2);
  xor xor_27 (out_5[26], dff_27_out_2, and_125_out);
  and and_126 (and_126_out, and_125_out, dff_27_out_2);
  xor xor_28 (out_5[27], dff_28_out_2, and_126_out);
  and and_127 (and_127_out, and_126_out, dff_28_out_2);
  xor xor_29 (out_5[28], dff_29_out_2, and_127_out);
  and and_128 (and_128_out, and_127_out, dff_29_out_2);
  xor xor_30 (out_5[29], dff_30_out_2, and_128_out);
  and and_129 (and_129_out, and_128_out, dff_30_out_2);
  xor xor_31 (out_5[30], dff_31_out_2, and_129_out);
  and and_130 (and_130_out, and_129_out, dff_31_out_2);
  xor xor_32 (out_5[31], dff_32_out_2, and_130_out);
endmodule

module dff (
  input  in_1,
  output out_2
);

  wire clock_1_out, nand_1_out, nand_2_out, nand_3_out, nand_4_out, nand_5_out, nand_6_out, nand_7_out,
       not_1_out, not_2_out;

  Clock clock_1 (.out(clock_1_out));
  not not_1 (not_1_out, in_1);
  nand nand_1 (nand_1_out, in_1, clock_1_out);
  nand nand_2 (nand_2_out, nand_1_out, nand_4_out);
  nand nand_3 (nand_3_out, clock_1_out, not_1_out);
  nand nand_4 (nand_4_out, nand_2_out, nand_3_out);
  not not_2 (not_2_out, clock_1_out);
  nand nand_5 (nand_5_out, not_2_out, nand_4_out);
  nand nand_6 (nand_6_out, nand_2_out, not_2_out);
  nand nand_7 (nand_7_out, nand_5_out, out_2);
  nand nand_8 (out_2, nand_7_out, nand_6_out);
endmodule

module mux (
  input  in_1,
  input  in_2,
  input  in_3,
  output out_4
);

  wire and_1_out, and_2_out, not_1_out;

  not not_1 (not_1_out, in_1);
  and and_1 (and_1_out, not_1_out, in_2);
  or or_1 (out_4, and_1_out, and_2_out);
  and and_2 (and_2_out, in_1, in_3);
endmodule

module add (
  input  in_1,
  input  in_2,
  input  in_3,
  output out_4,
  output out_5
);

  wire and_1_out, xor_2_out;

  xor xor_1 (out_4, in_1, xor_2_out);
  xor xor_2 (xor_2_out, in_2, in_3);
  or or_1 (out_5, in_1, and_1_out);
  and and_1 (and_1_out, in_2, in_3);
endmodule

module ALU (
  input  [31:0] a,
  input  [31:0] b,
  input  mode0,
  input  mode1,
  input  sub,
  input  arith,
  input  logic0,
  input  logic1,
  output [31:0] result,
  output zero,
  output neg
);

  wire add_and_or_1_carry, and_1_out, mux_1_out_4, not_1_out, or_1_out, or_2_out, or_3_out, or_4_out,
       or_5_out, or_6_out, or_7_out, or_8_out, or_9_out, or_10_out, or_11_out, or_12_out, or_13_out,
       or_14_out, or_15_out, or_16_out, or_17_out, or_18_out, or_19_out, or_20_out, or_21_out, or_22_out,
       or_23_out, or_24_out, or_25_out, or_26_out, or_27_out, or_28_out, or_29_out, or_30_out, or_31_out,
       or_32_out;
  wire [31:0] add_and_or_1_add_result, add_and_or_1_and_result, add_and_or_1_or_result,
       add_and_or_1_xor_result, mux32_1_out_4, mux32_2_out_4, mux32_3_out_4, mux32_5_out_4, mux32_6_out_4,
       mux32_7_out_4, mux32_8_out_4, not32_1_out_2, shift_1_result;

  and and_1 (and_1_out, mode0, mode1);
  or or_1 (or_1_out, and_1_out, sub);
  not32 not32_1 (.in_1(b), .out_2(not32_1_out_2));
  mux32 mux32_1 (.in_3(not32_1_out_2), .in_2(b), .in_1(or_1_out), .out_4(mux32_1_out_4));
  shift shift_1 (.right(sub), .arith(arith), .b(b[4:0]), .a(a), .result(shift_1_result));
  add_and_or add_and_or_1 (
    .b(mux32_1_out_4), .a(a), .neg(or_1_out), .xor_result(add_and_or_1_xor_result),
    .add_result(add_and_or_1_add_result), .and_result(add_and_or_1_and_result),
    .or_result(add_and_or_1_or_result), .carry(add_and_or_1_carry));
  not not_1 (not_1_out, add_and_or_1_carry);
  mux mux_1 (.in_2(add_and_or_1_add_result[31]), .in_3(not_1_out), .in_1(arith), .out_4(mux_1_out_4));
  mux32 mux32_2 (.in_3(32'h1), .in_2({32{1'b0}}), .in_1(mux_1_out_4), .out_4(mux32_2_out_4));
  mux32 mux32_3 (.in_3(mux32_6_out_4), .in_2(add_and_or_1_add_result), .in_1(mode0), .out_4(mux32_3_out_4));
  mux32 mux32_4 (.in_3(mux32_8_out_4), .in_2(mux32_3_out_4), .in_1(mode1), .out_4({neg, result[30:0]}));
  mux32 mux32_5 (.in_3(add_and_or_1_or_result), .in_2(add_and_or_1_and_result), .in_1(logic0), .out_4(mux32_5_out_4));
  mux32 mux32_6 (.in_3(mux32_7_out_4), .in_2(mux32_5_out_4), .in_1(logic1), .out_4(mux32_6_out_4));
  mux32 mux32_7 (.in_3(b), .in_2(add_and_or_1_xor_result), .in_1(logic0), .out_4(mux32_7_out_4));
  mux32 mux32_8 (.in_3(mux32_2_out_4), .in_2(shift_1_result), .in_1(mode0), .out_4(mux32_8_out_4));
  or or_2 (or_2_out, result[0], result[1]);
  or or_3 (or_3_out, result[2], result[3]);
  or or_4 (or_4_out, result[4], result[5]);
  or or_5 (or_5_out, result[6], result[7]);
  or or_6 (or_6_out, result[8], result[9]);
  or or_7 (or_7_out, result[10], result[11]);
  or or_8 (or_8_out, result[12], result[13]);
  or or_9 (or_9_out, result[14], result[15]);
  or or_10 (or_10_out, result[16], result[17]);
  or or_11 (or_11_out, result[18], result[19]);
  or or_12 (or_12_out, result[20], result[21]);
  or or_13 (or_13_out, result[22], result[23]);
  or or_14 (or_14_out, result[24], result[25]);
  or or_15 (or_15_out, result[26], result[27]);
  or or_16 (or_16_out, result[28], result[29]);
  or or_17 (or_17_out, result[30], neg);
  or or_18 (or_18_out, or_2_out, or_3_out);
  or or_19 (or_19_out, or_18_out, or_20_out);
  or or_20 (or_20_out, or_4_out, or_5_out);
  or or_21 (or_21_out, or_19_out, or_23_out);
  or or_22 (or_22_out, or_6_out, or_7_out);
  or or_23 (or_23_out, or_22_out, or_24_out);
  or or_24 (or_24_out, or_8_out, or_9_out);
  not not_2 (zero, or_25_out);
  or or_25 (or_25_out, or_21_out, or_29_out);
  or or_26 (or_26_out, or_10_out, or_11_out);
  or or_27 (or_27_out, or_26_out, or_28_out);
  or or_28 (or_28_out, or_12_out, or_13_out);
  or or_29 (or_29_out, or_27_out, or_31_out);
  or or_30 (or_30_out, or_14_out, or_15_out);
  or or_31 (or_31_out, or_30_out, or_32_out);
  or or_32 (or_32_out, or_16_out, or_17_out);

  assign result[31] = neg;
endmodule

module select_register (
  input  [4:0] rs1,
  input  load1,
  input  [4:0] rs2,
  input  load2,
  input  [4:0] rd,
  input  store,
  input  [31:0] in1,
  output [31:0] out1,
  output [31:0] out2
);
endmodule

module \bit  (
  input  in_1,
  input  in_2,
  output out_3
);

  wire and_1_out, and_2_out, not_1_out, or_1_out;

  not not_1 (not_1_out, in_1);
  and and_1 (and_1_out, not_1_out, in_2);
  or or_1 (or_1_out, and_1_out, and_2_out);
  and and_2 (and_2_out, in_1, out_3);
  dff dff_1 (.in_1(or_1_out), .out_2(out_3));
endmodule

module mux5 (
  input  in_1,
  input  [4:0] in_2,
  input  [4:0] in_3,
  output [4:0] out_4
);

  wire and_1_out, and_2_out, and_3_out, and_4_out, and_5_out, and_6_out, and_7_out, and_8_out, and_9_out,
       and_10_out, not_1_out;

  not not_1 (not_1_out, in_1);
  and and_1 (and_1_out, not_1_out, in_2[0]);
  and and_2 (and_2_out, in_1, in_3[0]);
  and and_3 (and_3_out, not_1_out, in_2[1]);
  and and_4 (and_4_out, in_1, in_3[1]);
  and and_5 (and_5_out, not_1_out, in_2[2]);
  and and_6 (and_6_out, in_1, in_3[2]);
  and and_7 (and_7_out, not_1_out, in_2[3]);
  and and_8 (and_8_out, in_1, in_3[3]);
  and and_9 (and_9_out, not_1_out, in_2[4]);
  and and_10 (and_10_out, in_1, in_3[4]);
  or or_1 (out_4[0], and_1_out, and_2_out);
  or or_2 (out_4[1], and_3_out, and_4_out);
  or or_3 (out_4[2], and_5_out, and_6_out);
  or or_4 (out_4[3], and_7_out, and_8_out);
  or or_5 (out_4[4], and_9_out, and_10_out);
endmodule

module mux12 (
  input  in_1,
  input  [11:0] in_2,
  input  [11:0] in_3,
  output [11:0] out_4
);

  wire and_1_out, and_2_out, and_3_out, and_4_out, and_5_out, and_6_out, and_7_out, and_8_out, and_9_out,
       and_10_out, and_11_out, and_12_out, and_13_out, and_14_out, and_15_out, and_16_out, and_17_out,
       and_18_out, and_19_out, and_20_out, and_21_out, and_22_out, and_23_out, and_24_out, not_1_out;

  not not_1 (not_1_out, in_1);
  and and_1 (and_1_out, not_1_out, in_2[0]);
  or or_1 (out_4[0], and_1_out, and_2_out);
  and and_2 (and_2_out, in_1, in_3[0]);
  and and_3 (and_3_out, not_1_out, in_2[1]);
  or or_2 (out_4[1], and_3_out, and_4_out);
  and and_4 (and_4_out, in_1, in_3[1]);
  and and_5 (and_5_out, not_1_out, in_2[2]);
  or or_3 (out_4[2], and_5_out, and_6_out);
  and and_6 (and_6_out, in_1, in_3[2]);
  and and_7 (and_7_out, not_1_out, in_2[3]);
  or or_4 (out_4[3], and_7_out, and_8_out);
  and and_8 (and_8_out, in_1, in_3[3]);
  and and_9 (and_9_out, not_1_out, in_2[4]);
  or or_5 (out_4[4], and_9_out, and_10_out);
  and and_10 (and_10_out, in_1, in_3[4]);
  and and_11 (and_11_out, not_1_out, in_2[5]);
  or or_6 (out_4[5], and_11_out, and_12_out);
  and and_12 (and_12_out, in_1, in_3[5]);
  and and_13 (and_13_out, not_1_out, in_2[6]);
  or or_7 (out_4[6], and_13_out, and_14_out);
  and and_14 (and_14_out, in_1, in_3[6]);
  and and_15 (and_15_out, not_1_out, in_2[7]);
  or or_8 (out_4[7], and_15_out, and_16_out);
  and and_16 (and_16_out, in_1, in_3[7]);
  and and_17 (and_17_out, not_1_out, in_2[8]);
  or or_9 (out_4[8], and_17_out, and_18_out);
  and and_18 (and_18_out, in_1, in_3[8]);
  and and_19 (and_19_out, not_1_out, in_2[9]);
  or or_10 (out_4[9], and_19_out, and_20_out);
  and and_20 (and_20_out, in_1, in_3[9]);
  and and_21 (and_21_out, not_1_out, in_2[10]);
  or or_11 (out_4[10], and_21_out, and_22_out);
  and and_22 (and_22_out, in_1, in_3[10]);
  and and_23 (and_23_out, not_1_out, in_2[11]);
  or or_12 (out_4[11], and_23_out, and_24_out);
  and and_24 (and_24_out, in_1, in_3[11]);
endmodule

module mux32 (
  input  in_1,
  input  [31:0] in_2,
  input  [31:0] in_3,
  output [31:0] out_4
);

  wire and_1_out, and_2_out, and_3_out, and_4_out, and_5_out, and_6_out, and_7_out, and_8_out, and_9_out,
       and_10_out, and_11_out, and_12_out, and_13_out, and_14_out, and_15_out, and_16_out, and_17_out,
       and_18_out, and_19_out, and_20_out, and_21_out, and_22_out, and_23_out, and_24_out, and_25_out,
       and_26_out, and_27_out, and_28_out, and_29_out, and_30_out, and_31_out, and_32_out, and_33_out,
       and_34_out, and_35_out, and_36_out, and_37_out, and_38_out, and_39_out, and_40_out, and_41_out,
       and_42_out, and_43_out, and_44_out, and_45_out, and_46_out, and_47_out, and_48_out, and_49_out,
       and_50_out, and_51_out, and_52_out, and_53_out, and_54_out, and_55_out, and_56_out, and_57_out,
       and_58_out, and_59_out, and_60_out, and_61_out, and_62_out, and_63_out, and_64_out, not_1_out;

  not not_1 (not_1_out, in_1);
  and and_1 (and_1_out, not_1_out, in_2[0]);
  and and_2 (and_2_out, in_1, in_3[0]);
  and and_3 (and_3_out, not_1_out, in_2[1]);
  and and_4 (and_4_out, in_1, in_3[1]);
  and and_5 (and_5_out, not_1_out, in_2[2]);
  and and_6 (and_6_out, in_1, in_3[2]);
  and and_7 (and_7_out, not_1_out, in_2[3]);
  and and_8 (and_8_out, in_1, in_3[3]);
  and and_9 (and_9_out, not_1_out, in_2[4]);
  and and_10 (and_10_out, in_1, in_3[4]);
  and and_11 (and_11_out, not_1_out, in_2[5]);
  and and_12 (and_12_out, in_1, in_3[5]);
  and and_13 (and_13_out, not_1_out, in_2[6]);
  and and_14 (and_14_out, in_1, in_3[6]);
  and and_15 (and_15_out, not_1_out, in_2[7]);
  and and_16 (and_16_out, in_1, in_3[7]);
  and and_17 (and_17_out, not_1_out, in_2[8]);
  and and_18 (and_18_out, in_1, in_3[8]);
  and and_19 (and_19_out, not_1_out, in_2[9]);
  and and_20 (and_20_out, in_1, in_3[9]);
  and and_21 (and_21_out, not_1_out, in_2[10]);
  and and_22 (and_22_out, in_1, in_3[10]);
  and and_23 (and_23_out, not_1_out, in_2[11]);
  and and_24 (and_24_out, in_1, in_3[11]);
  and and_25 (and_25_out, not_1_out, in_2[12]);
  and and_26 (and_26_out, in_1, in_3[12]);
  and and_27 (and_27_out, not_1_out, in_2[13]);
  and and_28 (and_28_out, in_1, in_3[13]);
  and and_29 (and_29_out, not_1_out, in_2[14]);
  and and_30 (and_30_out, in_1, in_3[14]);
  and and_31 (and_31_out, not_1_out, in_2[15]);
  and and_32 (and_32_out, in_1, in_3[15]);
  and and_33 (and_33_out, not_1_out, in_2[16]);
  and and_34 (and_34_out, in_1, in_3[16]);
  and and_35 (and_35_out, not_1_out, in_2[17]);
  and and_36 (and_36_out, in_1, in_3[17]);
  and and_37 (and_37_out, not_1_out, in_2[18]);
  and and_38 (and_38_out, in_1, in_3[18]);
  and and_39 (and_39_out, not_1_out, in_2[19]);
  and and_40 (and_40_out, in_1, in_3[19]);
  and and_41 (and_41_out, not_1_out, in_2[20]);
  and and_42 (and_42_out, in_1, in_3[20]);
  and and_43 (and_43_out, not_1_out, in_2[21]);
  and and_44 (and_44_out, in_1, in_3[21]);
  and and_45 (and_45_out, not_1_out, in_2[22]);
  and and_46 (and_46_out, in_1, in_3[22]);
  and and_47 (and_47_out, not_1_out, in_2[23]);
  and and_48 (and_48_out, in_1, in_3[23]);
  and and_49 (and_49_out, not_1_out, in_2[24]);
  and and_50 (and_50_out, in_1, in_3[24]);
  and and_51 (and_51_out, not_1_out, in_2[25]);
  and and_52 (and_52_out, in_1, in_3[25]);
  and and_53 (and_53_out, not_1_out, in_2[26]);
  and and_54 (and_54_out, in_1, in_3[26]);
  and and_55 (and_55_out, not_1_out, in_2[27]);
  and and_56 (and_56_out, in_1, in_3[27]);
  and and_57 (and_57_out, not_1_out, in_2[28]);
  and and_58 (and_58_out, in_1, in_3[28]);
  and and_59 (and_59_out, not_1_out, in_2[29]);
  and and_60 (and_60_out, in_1, in_3[29]);
  and and_61 (and_61_out, not_1_out, in_2[30]);
  and and_62 (and_62_out, in_1, in_3[30]);
  and and_63 (and_63_out, not_1_out, in_2[31]);
  and and_64 (and_64_out, in_1, in_3[31]);
  or or_1 (out_4[0], and_1_out, and_2_out);
  or or_2 (out_4[1], and_3_out, and_4_out);
  or or_3 (out_4[2], and_5_out, and_6_out);
  or or_4 (out_4[3], and_7_out, and_8_out);
  or or_5 (out_4[4], and_9_out, and_10_out);
  or or_6 (out_4[5], and_11_out, and_12_out);
  or or_7 (out_4[6], and_13_out, and_14_out);
  or or_8 (out_4[7], and_15_out, and_16_out);
  or or_9 (out_4[8], and_17_out, and_18_out);
  or or_10 (out_4[9], and_19_out, and_20_out);
  or or_11 (out_4[10], and_21_out, and_22_out);
  or or_12 (out_4[11], and_23_out, and_24_out);
  or or_13 (out_4[12], and_25_out, and_26_out);
  or or_14 (out_4[13], and_27_out, and_28_out);
  or or_15 (out_4[14], and_29_out, and_30_out);
  or or_16 (out_4[15], and_31_out, and_32_out);
  or or_17 (out_4[16], and_33_out, and_34_out);
  or or_18 (out_4[17], and_35_out, and_36_out);
  or or_19 (out_4[18], and_37_out, and_38_out);
  or or_20 (out_4[19], and_39_out, and_40_out);
  or or_21 (out_4[20], and_41_out, and_42_out);
  or or_22 (out_4[21], and_43_out, and_44_out);
  or or_23 (out_4[22], and_45_out, and_46_out);
  or or_24 (out_4[23], and_47_out, and_48_out);
  or or_25 (out_4[24], and_49_out, and_50_out);
  or or_26 (out_4[25], and_51_out, and_52_out);
  or or_27 (out_4[26], and_53_out, and_54_out);
  or or_28 (out_4[27], and_55_out, and_56_out);
  or or_29 (out_4[28], and_57_out, and_58_out);
  or or_30 (out_4[29], and_59_out, and_60_out);
  or or_31 (out_4[30], and_61_out, and_62_out);
  or or_32 (out_4[31], and_63_out, and_64_out);
endmodule

module sign (
  input  [31:0] value,
  input  [3:0] read,
  input  unsign,
  output [31:0] result
);

  wire and_1_out, and_2_out, and_3_out, and_4_out, and_5_out, and_6_out, and_7_out, not_1_out, not_2_out,
       not_3_out, not_4_out, or_1_out, or_2_out, or_3_out;
  wire [7:0] mux8_1_out_4, mux8_2_out_4, mux8_3_out_4, mux8_4_out_4, mux8_5_out_4, mux8_6_out_4,
       mux8_7_out_4, mux8_12_out_4, mux8_13_out_4, mux8_14_out_4;

  and and_1 (and_1_out, read[3], read[2]);
  and and_2 (and_2_out, read[1], read[0]);
  not not_1 (not_1_out, read[0]);
  and and_3 (and_3_out, not_1_out, not_2_out);
  not not_2 (not_2_out, read[1]);
  not not_3 (not_3_out, read[2]);
  and and_4 (and_4_out, not_3_out, not_4_out);
  not not_4 (not_4_out, read[3]);
  and and_5 (and_5_out, and_1_out, and_2_out);
  or or_1 (or_1_out, read[2], read[3]);
  or or_2 (or_2_out, read[1], read[3]);
  and and_6 (and_6_out, and_1_out, and_3_out);
  or or_3 (or_3_out, and_6_out, and_7_out);
  and and_7 (and_7_out, and_4_out, and_2_out);
  mux8 mux8_1 (.in_1(or_2_out), .in_3(value[15:8]), .in_2(value[7:0]), .out_4(mux8_1_out_4));
  mux8 mux8_2 (.in_1(or_2_out), .in_3(value[31:24]), .in_2(value[23:16]), .out_4(mux8_2_out_4));
  mux8 mux8_3 (.in_1(or_1_out), .in_3(mux8_2_out_4), .in_2(mux8_1_out_4), .out_4(mux8_3_out_4));
  mux8 mux8_4 (.in_1(and_6_out), .in_3(value[23:16]), .in_2(value[7:0]), .out_4(mux8_4_out_4));
  mux8 mux8_5 (.in_1(and_6_out), .in_3(value[31:24]), .in_2(value[15:8]), .out_4(mux8_5_out_4));
  mux8 mux8_6 (.in_1(or_3_out), .in_3(mux8_4_out_4), .in_2(mux8_3_out_4), .out_4(mux8_6_out_4));
  mux8 mux8_7 (.in_1(or_3_out), .in_3(mux8_5_out_4), .in_2(mux8_12_out_4), .out_4(mux8_7_out_4));
  mux8 mux8_8 (.in_1(and_5_out), .in_3(value[7:0]), .in_2(mux8_6_out_4), .out_4(result[7:0]));
  mux8 mux8_9 (.in_1(and_5_out), .in_3(value[15:8]), .in_2(mux8_7_out_4), .out_4(result[15:8]));
  mux8 mux8_10 (.in_1(and_5_out), .in_3(value[23:16]), .in_2(mux8_14_out_4), .out_4(result[23:16]));
  mux8 mux8_11 (.in_1(and_5_out), .in_3(value[31:24]), .in_2(mux8_14_out_4), .out_4(result[31:24]));
  mux8 mux8_12 (.in_1(unsign), .in_3({8{1'b0}}), .in_2({8{mux8_3_out_4[7]}}), .out_4(mux8_12_out_4));
  mux8 mux8_13 (.in_1(unsign), .in_3({8{1'b0}}), .in_2({8{mux8_5_out_4[7]}}), .out_4(mux8_13_out_4));
  mux8 mux8_14 (.in_1(or_3_out), .in_3(mux8_13_out_4), .in_2(mux8_12_out_4), .out_4(mux8_14_out_4));
endmodule

module mux8 (
  input  in_1,
  input  [7:0] in_2,
  input  [7:0] in_3,
  output [7:0] out_4
);

  wire and_1_out, and_2_out, and_3_out, and_4_out, and_5_out, and_6_out, and_7_out, and_8_out, and_9_out,
       and_10_out, and_11_out, and_12_out, and_13_out, and_14_out, and_15_out, and_16_out, not_1_out;

  not not_1 (not_1_out, in_1);
  and and_1 (and_1_out, not_1_out, in_2[0]);
  or or_1 (out_4[0], and_1_out, and_2_out);
  and and_2 (and_2_out, in_1, in_3[0]);
  and and_3 (and_3_out, not_1_out, in_2[1]);
  or or_2 (out_4[1], and_3_out, and_4_out);
  and and_4 (and_4_out, in_1, in_3[1]);
  and and_5 (and_5_out, not_1_out, in_2[2]);
  or or_3 (out_4[2], and_5_out, and_6_out);
  and and_6 (and_6_out, in_1, in_3[2]);
  and and_7 (and_7_out, not_1_out, in_2[3]);
  or or_4 (out_4[3], and_7_out, and_8_out);
  and and_8 (and_8_out, in_1, in_3[3]);
  and and_9 (and_9_out, not_1_out, in_2[4]);
  or or_5 (out_4[4], and_9_out, and_10_out);
  and and_10 (and_10_out, in_1, in_3[4]);
  and and_11 (and_11_out, not_1_out, in_2[5]);
  or or_6 (out_4[5], and_11_out, and_12_out);
  and and_12 (and_12_out, in_1, in_3[5]);
  and and_13 (and_13_out, not_1_out, in_2[6]);
  or or_7 (out_4[6], and_13_out, and_14_out);
  and and_14 (and_14_out, in_1, in_3[6]);
  and and_15 (and_15_out, not_1_out, in_2[7]);
  or or_8 (out_4[7], and_15_out, and_16_out);
  and and_16 (and_16_out, in_1, in_3[7]);
endmodule

module add_and_or (
  input  neg,
  input  [31:0] a,
  input  [31:0] b,
  output [31:0] or_result,
  output [31:0] xor_result,
  output [31:0] add_result,
  output [31:0] and_result,
  output carry
);

  wire and_33_out, and_34_out, and_35_out, and_36_out, and_37_out, and_38_out, and_39_out, and_40_out,
       and_41_out, and_42_out, and_43_out, and_44_out, and_45_out, and_46_out, and_47_out, and_48_out,
       and_49_out, and_50_out, and_51_out, and_52_out, and_53_out, and_54_out, and_55_out, and_56_out,
       and_57_out, and_58_out, and_59_out, and_60_out, and_61_out, and_62_out, and_63_out, and_64_out,
       or_33_out, or_34_out, or_35_out, or_36_out, or_37_out, or_38_out, or_39_out, or_40_out, or_41_out,
       or_42_out, or_43_out, or_44_out, or_45_out, or_46_out, or_47_out, or_48_out, or_49_out, or_50_out,
       or_51_out, or_52_out, or_53_out, or_54_out, or_55_out, or_56_out, or_57_out, or_58_out, or_59_out,
       or_60_out, or_61_out, or_62_out, or_63_out;

  or or_1 (or_result[0], a[0], b[0]);
  xor xor_1 (xor_result[0], a[0], b[0]);
  and and_1 (and_result[0], b[0], a[0]);
  or or_2 (or_result[1], a[1], b[1]);
  xor xor_2 (xor_result[1], a[1], b[1]);
  and and_2 (and_result[1], b[1], a[1]);
  or or_3 (or_result[2], a[2], b[2]);
  xor xor_3 (xor_result[2], a[2], b[2]);
  and and_3 (and_result[2], b[2], a[2]);
  or or_4 (or_result[3], a[3], b[3]);
  xor xor_4 (xor_result[3], a[3], b[3]);
  and and_4 (and_result[3], b[3], a[3]);
  or or_5 (or_result[4], a[4], b[4]);
  xor xor_5 (xor_result[4], a[4], b[4]);
  and and_5 (and_result[4], b[4], a[4]);
  or or_6 (or_result[5], a[5], b[5]);
  xor xor_6 (xor_result[5], a[5], b[5]);
  and and_6 (and_result[5], b[5], a[5]);
  or or_7 (or_result[6], a[6], b[6]);
  xor xor_7 (xor_result[6], a[6], b[6]);
  and and_7 (and_result[6], b[6], a[6]);
  or or_8 (or_result[7], a[7], b[7]);
  xor xor_8 (xor_result[7], a[7], b[7]);
  and and_8 (and_result[7], b[7], a[7]);
  or or_9 (or_result[8], a[8], b[8]);
  xor xor_9 (xor_result[8], a[8], b[8]);
  and and_9 (and_result[8], b[8], a[8]);
  or or_10 (or_result[9], a[9], b[9]);
  xor xor_10 (xor_result[9], a[9], b[9]);
  and and_10 (and_result[9], b[9], a[9]);
  or or_11 (or_result[10], a[10], b[10]);
  xor xor_11 (xor_result[10], a[10], b[10]);
  and and_11 (and_result[10], b[10], a[10]);
  or or_12 (or_result[11], a[11], b[11]);
  xor xor_12 (xor_result[11], a[11], b[11]);
  and and_12 (and_result[11], b[11], a[11]);
  or or_13 (or_result[12], a[12], b[12]);
  xor xor_13 (xor_result[12], a[12], b[12]);
  and and_13 (and_result[12], b[12], a[12]);
  or or_14 (or_result[13], a[13], b[13]);
  xor xor_14 (xor_result[13], a[13], b[13]);
  and and_14 (and_result[13], b[13], a[13]);
  or or_15 (or_result[14], a[14], b[14]);
  xor xor_15 (xor_result[14], a[14], b[14]);
  and and_15 (and_result[14], b[14], a[14]);
  or or_16 (or_result[15], a[15], b[15]);
  xor xor_16 (xor_result[15], a[15], b[15]);
  and and_16 (and_result[15], b[15], a[15]);
  or or_17 (or_result[16], a[16], b[16]);
  xor xor_17 (xor_result[16], a[16], b[16]);
  and and_17 (and_result[16], b[16], a[16]);
  or or_18 (or_result[17], a[17], b[17]);
  xor xor_18 (xor_result[17], a[17], b[17]);
  and and_18 (and_result[17], b[17], a[17]);
  or or_19 (or_result[18], a[18], b[18]);
  xor xor_19 (xor_result[18], a[18], b[18]);
  and and_19 (and_result[18], b[18], a[18]);
  or or_20 (or_result[19], a[19], b[19]);
  xor xor_20 (xor_result[19], a[19], b[19]);
  and and_20 (and_result[19], b[19], a[19]);
  or or_21 (or_result[20], a[20], b[20]);
  xor xor_21 (xor_result[20], a[20], b[20]);
  and and_21 (and_result[20], b[20], a[20]);
  or or_22 (or_result[21], a[21], b[21]);
  xor xor_22 (xor_result[21], a[21], b[21]);
  and and_22 (and_result[21], b[21], a[21]);
  or or_23 (or_result[22], a[22], b[22]);
  xor xor_23 (xor_result[22], a[22], b[22]);
  and and_23 (and_result[22], b[22], a[22]);
  or or_24 (or_result[23], a[23], b[23]);
  xor xor_24 (xor_result[23], a[23], b[23]);
  and and_24 (and_result[23], b[23], a[23]);
  or or_25 (or_result[24], a[24], b[24]);
  xor xor_25 (xor_result[24], a[24], b[24]);
  and and_25 (and_result[24], b[24], a[24]);
  or or_26 (or_result[25], a[25], b[25]);
  xor xor_26 (xor_result[25], a[25], b[25]);
  and and_26 (and_result[25], b[25], a[25]);
  or or_27 (or_result[26], a[26], b[26]);
  xor xor_27 (xor_result[26], a[26], b[26]);
  and and_27 (and_result[26], b[26], a[26]);
  or or_28 (or_result[27], a[27], b[27]);
  xor xor_28 (xor_result[27], a[27], b[27]);
  and and_28 (and_result[27], b[27], a[27]);
  or or_29 (or_result[28], a[28], b[28]);
  xor xor_29 (xor_result[28], a[28], b[28]);
  and and_29 (and_result[28], b[28], a[28]);
  or or_30 (or_result[29], a[29], b[29]);
  xor xor_30 (xor_result[29], a[29], b[29]);
  and and_30 (and_result[29], b[29], a[29]);
  or or_31 (or_result[30], a[30], b[30]);
  xor xor_31 (xor_result[30], a[30], b[30]);
  and and_31 (and_result[30], b[30], a[30]);
  or or_32 (or_result[31], a[31], b[31]);
  xor xor_32 (xor_result[31], a[31], b[31]);
  and and_32 (and_result[31], b[31], a[31]);
  xor xor_33 (add_result[0], neg, xor_result[0]);
  and and_33 (and_33_out, neg, xor_result[0]);
  or or_33 (or_33_out, and_33_out, and_result[0]);
  xor xor_34 (add_result[1], or_33_out, xor_result[1]);
  and and_34 (and_34_out, or_33_out, xor_result[1]);
  or or_34 (or_34_out, and_34_out, and_result[1]);
  xor xor_35 (add_result[2], or_34_out, xor_result[2]);
  and and_35 (and_35_out, or_34_out, xor_result[2]);
  or or_35 (or_35_out, and_35_out, and_result[2]);
  xor xor_36 (add_result[3], or_35_out, xor_result[3]);
  and and_36 (and_36_out, or_35_out, xor_result[3]);
  or or_36 (or_36_out, and_36_out, and_result[3]);
  xor xor_37 (add_result[4], or_36_out, xor_result[4]);
  and and_37 (and_37_out, or_36_out, xor_result[4]);
  or or_37 (or_37_out, and_37_out, and_result[4]);
  xor xor_38 (add_result[5], or_37_out, xor_result[5]);
  and and_38 (and_38_out, or_37_out, xor_result[5]);
  or or_38 (or_38_out, and_38_out, and_result[5]);
  xor xor_39 (add_result[6], or_38_out, xor_result[6]);
  and and_39 (and_39_out, or_38_out, xor_result[6]);
  or or_39 (or_39_out, and_39_out, and_result[6]);
  xor xor_40 (add_result[7], or_39_out, xor_result[7]);
  and and_40 (and_40_out, or_39_out, xor_result[7]);
  or or_40 (or_40_out, and_40_out, and_result[7]);
  xor xor_41 (add_result[8], or_40_out, xor_result[8]);
  and and_41 (and_41_out, or_40_out, xor_result[8]);
  or or_41 (or_41_out, and_41_out, and_result[8]);
  xor xor_42 (add_result[9], or_41_out, xor_result[9]);
  and and_42 (and_42_out, or_41_out, xor_result[9]);
  or or_42 (or_42_out, and_42_out, and_result[9]);
  xor xor_43 (add_result[10], or_42_out, xor_result[10]);
  and and_43 (and_43_out, or_42_out, xor_result[10]);
  or or_43 (or_43_out, and_43_out, and_result[10]);
  xor xor_44 (add_result[11], or_43_out, xor_result[11]);
  and and_44 (and_44_out, or_43_out, xor_result[11]);
  or or_44 (or_44_out, and_44_out, and_result[11]);
  xor xor_45 (add_result[12], or_44_out, xor_result[12]);
  and and_45 (and_45_out, or_44_out, xor_result[12]);
  or or_45 (or_45_out, and_45_out, and_result[12]);
  xor xor_46 (add_result[13], or_45_out, xor_result[13]);
  and and_46 (and_46_out, or_45_out, xor_result[13]);
  or or_46 (or_46_out, and_46_out, and_result[13]);
  xor xor_47 (add_result[14], or_46_out, xor_result[14]);
  and and_47 (and_47_out, or_46_out, xor_result[14]);
  or or_47 (or_47_out, and_47_out, and_result[14]);
  xor xor_48 (add_result[15], or_47_out, xor_result[15]);
  and and_48 (and_48_out, or_47_out, xor_result[15]);
  or or_48 (or_48_out, and_48_out, and_result[15]);
  xor xor_49 (add_result[16], or_48_out, xor_result[16]);
  and and_49 (and_49_out, or_48_out, xor_result[16]);
  or or_49 (or_49_out, and_49_out, and_result[16]);
  xor xor_50 (add_result[17], or_49_out, xor_result[17]);
  and and_50 (and_50_out, or_49_out, xor_result[17]);
  or or_50 (or_50_out, and_50_out, and_result[17]);
  xor xor_51 (add_result[18], or_50_out, xor_result[18]);
  and and_51 (and_51_out, or_50_out, xor_result[18]);
  or or_51 (or_51_out, and_51_out, and_result[18]);
  xor xor_52 (add_result[19], or_51_out, xor_result[19]);
  and and_52 (and_52_out, or_51_out, xor_result[19]);
  or or_52 (or_52_out, and_52_out, and_result[19]);
  xor xor_53 (add_result[20], or_52_out, xor_result[20]);
  and and_53 (and_53_out, or_52_out, xor_result[20]);
  or or_53 (or_53_out, and_53_out, and_result[20]);
  xor xor_54 (add_result[21], or_53_out, xor_result[21]);
  and and_54 (and_54_out, or_53_out, xor_result[21]);
  or or_54 (or_54_out, and_54_out, and_result[21]);
  xor xor_55 (add_result[22], or_54_out, xor_result[22]);
  and and_55 (and_55_out, or_54_out, xor_result[22]);
  or or_55 (or_55_out, and_55_out, and_result[22]);
  xor xor_56 (add_result[23], or_55_out, xor_result[23]);
  and and_56 (and_56_out, or_55_out, xor_result[23]);
  or or_56 (or_56_out, and_56_out, and_result[23]);
  xor xor_57 (add_result[24], or_56_out, xor_result[24]);
  and and_57 (and_57_out, or_56_out, xor_result[24]);
  or or_57 (or_57_out, and_57_out, and_result[24]);
  xor xor_58 (add_result[25], or_57_out, xor_result[25]);
  and and_58 (and_58_out, or_57_out, xor_result[25]);
  or or_58 (or_58_out, and_58_out, and_result[25]);
  xor xor_59 (add_result[26], or_58_out, xor_result[26]);
  and and_59 (and_59_out, or_58_out, xor_result[26]);
  or or_59 (or_59_out, and_59_out, and_result[26]);
  xor xor_60 (add_result[27], or_59_out, xor_result[27]);
  and and_60 (and_60_out, or_59_out, xor_result[27]);
  or or_60 (or_60_out, and_60_out, and_result[27]);
  xor xor_61 (add_result[28], or_60_out, xor_result[28]);
  and and_61 (and_61_out, or_60_out, xor_result[28]);
  or or_61 (or_61_out, and_61_out, and_result[28]);
  xor xor_62 (add_result[29], or_61_out, xor_result[29]);
  and and_62 (and_62_out, or_61_out, xor_result[29]);
  or or_62 (or_62_out, and_62_out, and_result[29]);
  xor xor_63 (add_result[30], or_62_out, xor_result[30]);
  and and_63 (and_63_out, or_62_out, xor_result[30]);
  or or_63 (or_63_out, and_63_out, and_result[30]);
  xor xor_64 (add_result[31], or_63_out, xor_result[31]);
  and and_64 (and_64_out, or_63_out, xor_result[31]);
  or or_64 (carry, and_64_out, and_result[31]);
endmodule

module not32 (
  input  [31:0] in_1,
  output [31:0] out_2
);

  not not_1 (out_2[0], in_1[0]);
  not not_2 (out_2[1], in_1[1]);
  not not_3 (out_2[2], in_1[2]);
  not not_4 (out_2[3], in_1[3]);
  not not_5 (out_2[4], in_1[4]);
  not not_6 (out_2[5], in_1[5]);
  not not_7 (out_2[6], in_1[6]);
  not not_8 (out_2[7], in_1[7]);
  not not_9 (out_2[8], in_1[8]);
  not not_10 (out_2[9], in_1[9]);
  not not_11 (out_2[10], in_1[10]);
  not not_12 (out_2[11], in_1[11]);
  not not_13 (out_2[12], in_1[12]);
  not not_14 (out_2[13], in_1[13]);
  not not_15 (out_2[14], in_1[14]);
  not not_16 (out_2[15], in_1[15]);
  not not_17 (out_2[16], in_1[16]);
  not not_18 (out_2[17], in_1[17]);
  not not_19 (out_2[18], in_1[18]);
  not not_20 (out_2[19], in_1[19]);
  not not_21 (out_2[20], in_1[20]);
  not not_22 (out_2[21], in_1[21]);
  not not_23 (out_2[22], in_1[22]);
  not not_24 (out_2[23], in_1[23]);
  not not_25 (out_2[24], in_1[24]);
  not not_26 (out_2[25], in_1[25]);
  not not_27 (out_2[26], in_1[26]);
  not not_28 (out_2[27], in_1[27]);
  not not_29 (out_2[28], in_1[28]);
  not not_30 (out_2[29], in_1[29]);
  not not_31 (out_2[30], in_1[30]);
  not not_32 (out_2[31], in_1[31]);
endmodule

module shift (
  input  [4:0] b,
  input  [31:0] a,
  input  right,
  input  arith,
  output [31:0] result
);

  wire and_2_out;
  wire [31:0] mux32_1_out_4, mux32_2_out_4, mux32_3_out_4, mux32_4_out_4, mux32_5_out_4, mux32_6_out_4;
  wire [31:31] and_1_out;

  and and_1 (and_1_out[31], a[31], and_2_out);
  and and_2 (and_2_out, right, arith);
  mux32 mux32_1 (
    .in_3({a[0], a[1], a[2], a[3], a[4], a[5], a[6], a[7], a[8], a[9], a[10], a[11], a[12], a[13], a[14], a[15], a[16], a[17], a[18], a[19], a[20], a[21], a[22], a[23], a[24], a[25], a[26], a[27], a[28], a[29], a[30], a[31]}),
    .in_2(a), .in_1(right), .out_4(mux32_1_out_4));
  mux32 mux32_2 (.in_3({and_1_out[31], mux32_1_out_4[31:1]}), .in_2(mux32_1_out_4), .in_1(b[0]), .out_4(mux32_2_out_4));
  mux32 mux32_3 (
    .in_3({{2{and_1_out[31]}}, mux32_2_out_4[31:2]}), .in_2(mux32_2_out_4), .in_1(b[1]), .out_4(mux32_3_out_4));
  mux32 mux32_4 (
    .in_3({{4{and_1_out[31]}}, mux32_3_out_4[31:4]}), .in_2(mux32_3_out_4), .in_1(b[2]), .out_4(mux32_4_out_4));
  mux32 mux32_5 (
    .in_3({{8{and_1_out[31]}}, mux32_4_out_4[31:8]}), .in_2(mux32_4_out_4), .in_1(b[3]), .out_4(mux32_5_out_4));
  mux32 mux32_6 (
    .in_3({{16{and_1_out[31]}}, mux32_5_out_4[31:16]}), .in_2(mux32_5_out_4), .in_1(b[4]),
    .out_4(mux32_6_out_4));
  mux32 mux32_7 (
    .in_3({mux32_6_out_4[0], mux32_6_out_4[1], mux32_6_out_4[2], mux32_6_out_4[3], mux32_6_out_4[4], mux32_6_out_4[5], mux32_6_out_4[6], mux32_6_out_4[7], mux32_6_out_4[8], mux32_6_out_4[9], mux32_6_out_4[10], mux32_6_out_4[11], mux32_6_out_4[12], mux32_6_out_4[13], mux32_6_out_4[14], mux32_6_out_4[15], mux32_6_out_4[16], mux32_6_out_4[17], mux32_6_out_4[18], mux32_6_out_4[19], mux32_6_out_4[20], mux32_6_out_4[21], mux32_6_out_4[22], mux32_6_out_4[23], mux32_6_out_4[24], mux32_6_out_4[25], mux32_6_out_4[26], mux32_6_out_4[27], mux32_6_out_4[28], mux32_6_out_4[29], mux32_6_out_4[30], mux32_6_out_4[31]}),
    .in_2(mux32_6_out_4), .in_1(right), .out_4(result));
endmodule
